// Logisim project jrmips.circ as structural Verilog: 12 circuits, main circuit main
module main (
);

  wire branch_calc_out_2, clock_out, decoder1_1_alusrc, decoder1_1_signsrc, decoder2_loadmem,
       decoder2_regwrite, decoder2_shiftdirection, decoder2_storemem, fields_subop, not_1_out,
       put_halt_decoder_halt, put_halt_decoder_put;
  wire [1:0] decoder1_1_aluop, memToReg_out_3;
  wire [2:0] fields_source_register, fields_source_register_2, type_for_pc_pc_type;
  wire [3:0] fields_opcode, fields_shift_amount, put_register_hex1, put_register_hex2, put_register_hex3,
       put_register_hex4;
  wire [7:0] adder_1_out, fields_immediate, multiplexer_1_out, multiplexer_2_out, multiplexer_4_out,
       pc_Calc_rsforaddress, program_counter_q;
  wire [15:0] alu_result, bit_extender_1_out, bit_extender_2_out, bit_extender_3_out, multiplexer_3_out,
       multiplexer_5_out, multiplexer_6_out, multiplexer_7_out, ram_1_data, register_file_read_data_1,
       register_file_read_data_2, rom_1_data, shifter_1_out, shifter_2_out;

  Clock clock (.out(clock_out));
  Adder adder_1 (.a(8'h1), .b(program_counter_q), .out(adder_1_out), .cin(1'b0));  // open: cout
  Register program_counter (
    .D(multiplexer_4_out), .en(put_halt_decoder_halt), .Q(program_counter_q), .clk(clock_out));  // open: clr
  assign bit_extender_1_out = {{8{1'b0}}, adder_1_out};  // Bit_Extender bit_extender_1
  ROM #(.dataWidth(16)) rom_1 (.addr(program_counter_q), .data(rom_1_data), .sel(1'b1));
  branch_calc branch_calc (.Rs(register_file_read_data_1), .out_2(branch_calc_out_2));
  type_for_pc_register type_for_pc (.opcode(fields_opcode), .pc_type(type_for_pc_pc_type));
  put_halt_decoder put_halt_decoder (.opcode(fields_opcode), .put(put_halt_decoder_put), .halt(put_halt_decoder_halt));
  Fields fields (
    .Instruction(rom_1_data), .Opcode(fields_opcode), .Source_register(fields_source_register),
    .Source_register_2(fields_source_register_2), .shift_amount(fields_shift_amount), .subop(fields_subop),
    .Immediate(fields_immediate));
  Multiplexer #(.width(8), .enable("false")) multiplexer_1 (
    .in0(fields_immediate), .in1(adder_1_out), .out(multiplexer_1_out), .sel(branch_calc_out_2));
  Multiplexer #(.width(8), .enable("false")) multiplexer_2 (
    .in0(adder_1_out), .in1(fields_immediate), .out(multiplexer_2_out), .sel(branch_calc_out_2));
  Decoder1 decoder1_1 (
    .opcode(fields_opcode), .subop(fields_subop), .AluOp(decoder1_1_aluop), .AluSrc(decoder1_1_alusrc),
    .SignSrc(decoder1_1_signsrc));
  assign bit_extender_2_out = {{8{1'b0}}, fields_immediate};  // Bit_Extender bit_extender_2
  assign bit_extender_3_out = {{8{fields_immediate[7]}}, fields_immediate};  // Bit_Extender bit_extender_3
  not not_1 (not_1_out, put_halt_decoder_halt);
  LED led_1 (.in(not_1_out));
  Multiplexer #(.width(16), .enable("false")) multiplexer_3 (
    .in0(bit_extender_3_out), .in1(bit_extender_2_out), .out(multiplexer_3_out), .sel(decoder1_1_signsrc));
  Multiplexer #(.select(3), .width(8), .enable("false")) multiplexer_4 (
    .in0(adder_1_out), .in1(multiplexer_1_out), .in2(multiplexer_2_out), .in3(pc_Calc_rsforaddress),
    .in4(fields_immediate), .out(multiplexer_4_out), .sel(type_for_pc_pc_type));  // open: in5, in6, in7
  pc_Calc pc_Calc (.rs(register_file_read_data_1), .rsForAddress(pc_Calc_rsforaddress));
  registerfile register_file (
    .write_enable(decoder2_regwrite), .Read_Register_1(fields_source_register),
    .write_register(fields_source_register), .Read_Register_2(fields_source_register_2),
    .write_data(multiplexer_7_out), .in_6(clock_out), .Read_Data_1(register_file_read_data_1),
    .Read_data_2(register_file_read_data_2));
  Decoder2 decoder2 (
    .opcode(fields_opcode), .Subop(fields_subop), .RegWrite(decoder2_regwrite),
    .shiftDirection(decoder2_shiftdirection), .StoreMem(decoder2_storemem), .LoadMem(decoder2_loadmem));
  Multiplexer #(.width(16), .enable("false")) multiplexer_5 (
    .in0(register_file_read_data_2), .in1(multiplexer_3_out), .out(multiplexer_5_out), .sel(decoder1_1_alusrc));
  Shifter #(.width(16)) shifter_1 (.in(register_file_read_data_1), .\dist (fields_shift_amount), .out(shifter_1_out));
  Shifter #(.width(16), .shift("lr")) shifter_2 (
    .in(register_file_read_data_1), .\dist (fields_shift_amount), .out(shifter_2_out));
  put_register put_register (
    .enable_put(put_halt_decoder_put), .rs(register_file_read_data_1), .clock(clock_out),
    .hex1(put_register_hex1), .hex2(put_register_hex2), .hex3(put_register_hex3), .hex4(put_register_hex4));
  Alu alu (
    .input1(register_file_read_data_1), .input2(multiplexer_5_out), .operation(decoder1_1_aluop),
    .Result(alu_result));
  Hex_Digit_Display hex_digit_display_1 (.value(put_register_hex1));  // open: dp
  Multiplexer #(.width(16), .enable("false")) multiplexer_6 (
    .in0(shifter_1_out), .in1(shifter_2_out), .out(multiplexer_6_out), .sel(decoder2_shiftdirection));
  Hex_Digit_Display hex_digit_display_2 (.value(put_register_hex2));  // open: dp
  memToReg memToReg (.Subop(fields_subop), .opcode(fields_opcode), .out_3(memToReg_out_3));
  Hex_Digit_Display hex_digit_display_3 (.value(put_register_hex3));  // open: dp
  Hex_Digit_Display hex_digit_display_4 (.value(put_register_hex4));  // open: dp
  RAM #(.addrWidth(16), .dataWidth(16), .bus("separate")) ram_1 (
    .addr(register_file_read_data_2), .din(register_file_read_data_1), .data(ram_1_data),
    .str(decoder2_storemem), .sel(1'b1), .clk(clock_out), .ld(decoder2_loadmem));  // open: clr
  Multiplexer #(.select(2), .width(16), .enable("false")) multiplexer_7 (
    .in0(ram_1_data), .in1(alu_result), .in2(multiplexer_6_out), .in3(bit_extender_1_out),
    .out(multiplexer_7_out), .sel(memToReg_out_3));

  // Notes on the sheet:
  //   Alexander Ritov
  //   avr16@pitt.edu
endmodule

module Fields (
  input  [15:0] Instruction,
  output [3:0] Opcode,
  output [2:0] Source_register,
  output [2:0] Source_register_2,
  output [3:0] shift_amount,
  output subop,
  output [7:0] Immediate
);


  assign Immediate = Instruction[8:1];
  assign Opcode = Instruction[15:12];
  assign shift_amount = Instruction[4:1];
  assign Source_register = Instruction[11:9];
  assign Source_register_2 = Instruction[8:6];
  assign subop = Instruction[0];
endmodule

module Alu (
  input  [15:0] input1,
  input  [15:0] input2,
  input  [1:0] operation,
  output [15:0] Result
);

  wire [15:0] adder_1_out, and_1_out, and_2_out, not_1_out, not_2_out, subtractor_1_out;

  assign not_1_out = ~input1;  // NOT_Gate not_1, 16 bits wide
  assign not_2_out = ~input2;  // NOT_Gate not_2, 16 bits wide
  Adder #(.width(16)) adder_1 (.a(input1), .b(input2), .out(adder_1_out));  // open: cin, cout
  Subtractor #(.width(16)) subtractor_1 (.a(input1), .b(input2), .out(subtractor_1_out));  // open: bin, bout
  assign and_1_out = input1 & input2;  // AND_Gate and_1, 16 bits wide
  assign and_2_out = not_1_out & not_2_out;  // AND_Gate and_2, 16 bits wide
  Multiplexer #(.select(2), .width(16)) multiplexer_1 (
    .in0(adder_1_out), .in1(subtractor_1_out), .in2(and_1_out), .in3(and_2_out), .out(Result), .sel(operation));  // open: en
endmodule

module registerfile (
  input  write_enable,
  input  [2:0] Read_Register_1,
  input  [2:0] write_register,
  input  [2:0] Read_Register_2,
  input  [15:0] write_data,
  input  in_6,
  output [15:0] Read_Data_1,
  output [15:0] Read_data_2
);

  wire and_1_out, and_2_out, and_3_out, and_4_out, and_5_out, and_6_out, and_7_out, and_8_out,
       decoder_1_out0, decoder_1_out1, decoder_1_out2, decoder_1_out3, decoder_1_out4, decoder_1_out5,
       decoder_1_out6, decoder_1_out7;
  wire [15:0] register_1_q, register_2_q, register_3_q, register_4_q, register_5_q, register_6_q,
       register_7_q, register_8_q;

  Decoder #(.select(3)) decoder_1 (
    .out0(decoder_1_out0), .out1(decoder_1_out1), .out2(decoder_1_out2), .out3(decoder_1_out3),
    .out4(decoder_1_out4), .out5(decoder_1_out5), .out6(decoder_1_out6), .out7(decoder_1_out7),
    .sel(write_register));  // open: en
  and and_1 (and_1_out, write_enable, decoder_1_out0);
  and and_2 (and_2_out, write_enable, decoder_1_out1);
  and and_3 (and_3_out, write_enable, decoder_1_out2);
  and and_4 (and_4_out, write_enable, decoder_1_out3);
  and and_5 (and_5_out, write_enable, decoder_1_out4);
  and and_6 (and_6_out, write_enable, decoder_1_out5);
  and and_7 (and_7_out, write_enable, decoder_1_out6);
  and and_8 (and_8_out, write_enable, decoder_1_out7);
  Register #(.width(16)) register_1 (.D(write_data), .en(and_1_out), .Q(register_1_q), .clk(in_6));  // open: clr
  Register #(.width(16)) register_2 (.D(write_data), .en(and_2_out), .Q(register_2_q), .clk(in_6));  // open: clr
  Register #(.width(16)) register_3 (.D(write_data), .en(and_3_out), .Q(register_3_q), .clk(in_6));  // open: clr
  Register #(.width(16)) register_4 (.D(write_data), .en(and_4_out), .Q(register_4_q), .clk(in_6));  // open: clr
  Register #(.width(16)) register_5 (.D(write_data), .en(and_5_out), .Q(register_5_q), .clk(in_6));  // open: clr
  Register #(.width(16)) register_6 (.D(write_data), .en(and_6_out), .Q(register_6_q), .clk(in_6));  // open: clr
  Register #(.width(16)) register_7 (.D(write_data), .en(and_7_out), .Q(register_7_q), .clk(in_6));  // open: clr
  Register #(.width(16)) register_8 (.D(write_data), .en(and_8_out), .Q(register_8_q), .clk(in_6));  // open: clr
  Multiplexer #(.select(3), .width(16)) multiplexer_1 (
    .in0(register_1_q), .in1(register_2_q), .in2(register_3_q), .in3(register_4_q), .in4(register_5_q),
    .in5(register_6_q), .in6(register_7_q), .in7(register_8_q), .out(Read_Data_1), .sel(Read_Register_1));  // open: en
  Multiplexer #(.select(3), .width(16)) multiplexer_2 (
    .in0(register_1_q), .in1(register_2_q), .in2(register_3_q), .in3(register_4_q), .in4(register_5_q),
    .in5(register_6_q), .in6(register_7_q), .in7(register_8_q), .out(Read_data_2), .sel(Read_Register_2));  // open: en
endmodule

module put_register (
  input  enable_put,
  input  [15:0] rs,
  input  clock,
  output [3:0] hex1,
  output [3:0] hex2,
  output [3:0] hex3,
  output [3:0] hex4
);

  Register #(.width(16)) register_1 (.D(rs), .en(enable_put), .Q({hex1, hex2, hex3, hex4}), .clk(clock));  // open: clr
endmodule

module put_halt_decoder (
  input  [3:0] opcode,
  output put,
  output halt
);

  wire and_1_out, and_2_out, not_1_out, not_2_out, not_3_out, not_4_out, not_5_out, not_6_out, not_7_out,
       not_8_out, or_1_out, or_2_out;

  not not_1 (not_1_out, opcode[3]);
  and and_1 (and_1_out, not_1_out, not_2_out);
  not not_2 (not_2_out, opcode[2]);
  not not_3 (not_3_out, opcode[1]);
  and and_2 (and_2_out, not_3_out, not_4_out);
  not not_4 (not_4_out, opcode[0]);
  not not_5 (not_5_out, opcode[3]);
  or or_1 (or_1_out, not_5_out, not_6_out);
  not not_6 (not_6_out, opcode[2]);
  not not_7 (not_7_out, opcode[1]);
  or or_2 (or_2_out, not_7_out, not_8_out);
  not not_8 (not_8_out, opcode[0]);
  and and_3 (put, and_1_out, and_2_out);
  or or_3 (halt, or_1_out, or_2_out);
endmodule

module Decoder1 (
  input  [3:0] opcode,
  input  subop,
  output [1:0] AluOp,
  output AluSrc,
  output SignSrc
);

  and and_1 (AluOp[1], opcode[1], opcode[0]);
  and and_2 (AluOp[0], opcode[0], subop);
  not not_1 (AluSrc, opcode[0]);

  assign SignSrc = subop;
endmodule

module type_for_pc_register (
  input  [3:0] opcode,
  output [2:0] pc_type
);

  wire and_1_out, and_2_out, and_4_out, and_5_out, not_1_out, not_2_out, not_3_out, not_4_out, not_5_out,
       not_6_out;

  not not_1 (not_1_out, opcode[2]);
  not not_2 (not_2_out, opcode[1]);
  not not_3 (not_3_out, opcode[1]);
  and and_1 (and_1_out, opcode[3], not_3_out, opcode[0]);
  and and_2 (and_2_out, opcode[3], opcode[1], not_4_out);
  not not_4 (not_4_out, opcode[0]);
  and and_3 (pc_type[0], opcode[3], not_5_out, not_6_out);
  not not_5 (not_5_out, opcode[2]);
  not not_6 (not_6_out, opcode[0]);
  and and_4 (and_4_out, opcode[3], not_1_out, opcode[1], opcode[0]);
  or or_1 (pc_type[2], and_4_out, and_5_out);
  and and_5 (and_5_out, opcode[3], opcode[2], not_2_out);
  or or_2 (pc_type[1], and_1_out, and_2_out);
endmodule

module pc_Calc (
  input  [15:0] rs,
  output [7:0] rsForAddress
);


  assign rsForAddress = rs[7:0];
endmodule

module branch_calc (
  input  [15:0] Rs,
  output out_2
);

  Comparator #(.width(16)) comparator_1 (.a({16{1'b0}}), .b(Rs), .eq(out_2));  // open: gt, lt
endmodule

module Decoder2 (
  input  [3:0] opcode,
  input  Subop,
  output RegWrite,
  output shiftDirection,
  output StoreMem,
  output LoadMem
);

  wire and_1_out, and_2_out, and_3_out, and_4_out, and_5_out, and_6_out, and_7_out, and_8_out, and_9_out,
       and_10_out, and_11_out, and_12_out, and_13_out, and_14_out, and_15_out, and_16_out, not_1_out,
       not_2_out, not_3_out, not_4_out, not_5_out, not_6_out, not_7_out, not_8_out, not_9_out, not_10_out,
       not_11_out, not_12_out, not_13_out, not_14_out, or_1_out, or_2_out, or_3_out;

  not not_1 (not_1_out, opcode[3]);
  not not_2 (not_2_out, opcode[2]);
  not not_3 (not_3_out, opcode[3]);
  not not_4 (not_4_out, opcode[2]);
  not not_5 (not_5_out, opcode[3]);
  not not_6 (not_6_out, opcode[1]);
  not not_7 (not_7_out, opcode[3]);
  not not_8 (not_8_out, opcode[3]);
  not not_9 (not_9_out, Subop);
  and and_1 (and_1_out, not_1_out, not_2_out);
  and and_2 (and_2_out, not_3_out, not_4_out);
  not not_10 (not_10_out, opcode[2]);
  not not_11 (not_11_out, opcode[3]);
  not not_12 (not_12_out, opcode[3]);
  and and_3 (and_3_out, not_5_out, opcode[2]);
  and and_4 (and_4_out, not_6_out, Subop);
  and and_5 (and_5_out, not_7_out, opcode[2]);
  and and_6 (and_6_out, opcode[1], Subop);
  and and_7 (and_7_out, not_8_out, opcode[2]);
  and and_8 (and_8_out, opcode[1], not_9_out);
  and and_9 (and_9_out, and_1_out, opcode[0]);
  or or_1 (or_1_out, and_9_out, and_10_out);
  and and_10 (and_10_out, and_2_out, opcode[1]);
  and and_11 (and_11_out, not_10_out, opcode[1]);
  and and_12 (and_12_out, and_11_out, opcode[0]);
  and and_13 (and_13_out, not_11_out, opcode[2]);
  and and_14 (and_14_out, and_13_out, not_13_out);
  not not_13 (not_13_out, opcode[1]);
  and and_15 (and_15_out, not_12_out, opcode[2]);
  and and_16 (and_16_out, and_15_out, not_14_out);
  not not_14 (not_14_out, Subop);
  and and_17 (shiftDirection, and_3_out, and_4_out);
  and and_18 (StoreMem, and_5_out, and_6_out);
  and and_19 (LoadMem, and_7_out, and_8_out);
  or or_2 (or_2_out, or_1_out, and_12_out);
  or or_3 (or_3_out, and_14_out, and_16_out);
  or or_4 (RegWrite, or_2_out, or_3_out);
endmodule

module memToReg (
  input  Subop,
  input  [3:0] opcode,
  output [1:0] out_3
);

  wire and_1_out, and_2_out, and_3_out, and_4_out, and_5_out, and_6_out, and_7_out, and_8_out, and_9_out,
       and_10_out, and_11_out, not_1_out, not_2_out, not_3_out, not_4_out, not_5_out, not_6_out, not_7_out,
       not_8_out, or_2_out;

  not not_1 (not_1_out, opcode[3]);
  not not_2 (not_2_out, opcode[2]);
  not not_3 (not_3_out, opcode[3]);
  not not_4 (not_4_out, opcode[2]);
  not not_5 (not_5_out, opcode[3]);
  not not_6 (not_6_out, opcode[2]);
  and and_1 (and_1_out, not_1_out, opcode[2]);
  not not_7 (not_7_out, opcode[1]);
  and and_2 (and_2_out, opcode[3], not_2_out);
  and and_3 (and_3_out, opcode[1], opcode[0]);
  and and_4 (and_4_out, not_3_out, not_4_out);
  and and_5 (and_5_out, not_5_out, not_6_out);
  not not_8 (not_8_out, opcode[2]);
  and and_6 (and_6_out, and_1_out, not_7_out);
  or or_1 (out_3[1], and_6_out, and_7_out);
  and and_7 (and_7_out, and_2_out, and_3_out);
  and and_8 (and_8_out, and_4_out, opcode[0]);
  or or_2 (or_2_out, and_8_out, and_9_out);
  and and_9 (and_9_out, and_5_out, opcode[1]);
  and and_10 (and_10_out, not_8_out, opcode[1]);
  and and_11 (and_11_out, and_10_out, opcode[0]);
  or or_3 (out_3[0], or_2_out, and_11_out);
endmodule
